# Fritzing sketch ulli (saved by Fritzing 0.8.5b)

parts:
  Componente1 = Arduino Uno (Rev3)
  Componente2 = SRF05 Ultrasonic Rangefinder
  IC1 = L298 Dual Full Bridge Driver
  J1 = Basic Servo

nets:
  N1: Componente1.A0, J1.pulse
  N2: Componente1.D11_PWM/MOSI, Componente2.VCC
  N3: Componente1.D12/MISO, Componente2.Trig
  N4: Componente1.D13/SCK, Componente2.Echo
  GND: Componente1.GND, Componente2.GND, J1.gnd
  N5: Componente1.D2, IC1.pin11
  N6: Componente1.D3_PWM, IC1.pin12
  N7: Componente1.D4, IC1.pin10
  N8: Componente1.D5_PWM, IC1.pin7
  N9: Componente1.D6_PWM, IC1.pin5
  N10: Componente1.D7, IC1.pin6
  5V: Componente1.5V, J1.vcc

custom parts:
  L298 Dual Full Bridge Driver: L298 Dual Full Bridge Driver in a 15 lead Multiwatt package.
